// Digital circuit flip_flop.dig as structural Verilog
module flip_flop (
  input  D,
  input  C,
  output Q,
  output Qs
);

  wire and_1_out, and_2_out, and_3_out, and_4_out, nor_2_out, nor_4_out, not_1_out, not_2_out, not_3_out;

  not not_1 (not_1_out, D);
  and and_1 (and_1_out, not_1_out, C);
  and and_2 (and_2_out, C, D);
  nor nor_1 (Qs, and_1_out, nor_2_out);
  nor nor_2 (nor_2_out, Qs, and_2_out);
  not not_2 (not_2_out, C);
  not not_3 (not_3_out, Qs);
  and and_3 (and_3_out, not_3_out, not_2_out);
  and and_4 (and_4_out, not_2_out, Qs);
  nor nor_3 (Q, and_3_out, nor_4_out);
  nor nor_4 (nor_4_out, Q, and_4_out);
endmodule
