// Digital circuit latch_sr_en.dig as structural Verilog
module latch_sr_en (
  input  R,
  input  S,
  input  C,
  output Q,
  output nQ
);

  wire and_1_out, and_2_out;

  and and_1 (and_1_out, R, C);
  and and_2 (and_2_out, C, S);
  nor nor_1 (Q, and_1_out, nQ);
  nor nor_2 (nQ, Q, and_2_out);
endmodule
