// Digital circuit lsr.dig as structural Verilog
module lsr (
  input  DIN,
  input  clk
);

  wire d_ff_1_q, d_ff_2_q, d_ff_3_q, d_ff_4_q, d_ff_5_q;

  // Probe ASL on d_ff_1_q
  D_FF d_ff_1 (.D(d_ff_2_q), .C(clk), .Q(d_ff_1_q));  // open: nQ
  // Probe BSL on d_ff_2_q
  D_FF d_ff_2 (.D(d_ff_3_q), .C(clk), .Q(d_ff_2_q));  // open: nQ
  // Probe CSL on d_ff_3_q
  D_FF d_ff_3 (.D(d_ff_4_q), .C(clk), .Q(d_ff_3_q));  // open: nQ
  // Probe DSL on d_ff_4_q
  D_FF d_ff_4 (.D(d_ff_5_q), .C(clk), .Q(d_ff_4_q));  // open: nQ
  // Probe ESL on d_ff_5_q
  D_FF d_ff_5 (.D(DIN), .C(clk), .Q(d_ff_5_q));  // open: nQ
endmodule
