// Digital circuit register.dig as structural Verilog
module register (
  input  INA,
  input  INB,
  input  INC,
  input  IND,
  input  INE,
  input  clk
);

  wire d_ff_1_q, d_ff_2_q, d_ff_3_q, d_ff_4_q, d_ff_5_q;

  D_FF d_ff_1 (.D(INA), .C(clk), .Q(d_ff_1_q));  // open: nQ
  D_FF d_ff_2 (.D(INB), .C(clk), .Q(d_ff_2_q));  // open: nQ
  D_FF d_ff_3 (.D(INC), .C(clk), .Q(d_ff_3_q));  // open: nQ
  D_FF d_ff_4 (.D(IND), .C(clk), .Q(d_ff_4_q));  // open: nQ
  D_FF d_ff_5 (.D(INE), .C(clk), .Q(d_ff_5_q));  // open: nQ
  // Probe A on d_ff_1_q
  // Probe B on d_ff_2_q
  // Probe C on d_ff_3_q
  // Probe D on d_ff_4_q
  // Probe E on d_ff_5_q
endmodule
