// Digital circuit rsr.dig as structural Verilog
module rsr (
  input  clk,
  input  DIN
);

  wire d_ff_1_q, d_ff_2_q, d_ff_3_q, d_ff_4_q, d_ff_5_q;

  // Probe ASR on d_ff_1_q
  D_FF d_ff_1 (.D(DIN), .C(clk), .Q(d_ff_1_q));  // open: nQ
  // Probe BSR on d_ff_2_q
  D_FF d_ff_2 (.D(d_ff_1_q), .C(clk), .Q(d_ff_2_q));  // open: nQ
  // Probe CSR on d_ff_3_q
  D_FF d_ff_3 (.D(d_ff_2_q), .C(clk), .Q(d_ff_3_q));  // open: nQ
  // Probe DSR on d_ff_4_q
  D_FF d_ff_4 (.D(d_ff_3_q), .C(clk), .Q(d_ff_4_q));  // open: nQ
  // Probe ESR on d_ff_5_q
  D_FF d_ff_5 (.D(d_ff_4_q), .C(clk), .Q(d_ff_5_q));  // open: nQ
endmodule
