// Digital circuit rsr_charge.dig as structural Verilog
module rsr_charge (
  input  DIN,
  input  INA,
  input  INB,
  input  INC,
  input  IND,
  input  INE,
  input  LOAD,
  input  CLK
);

  wire d_ff_1_q, d_ff_2_q, d_ff_3_q, d_ff_4_q, d_ff_5_q, multiplexer_1_out, multiplexer_2_out,
       multiplexer_3_out, multiplexer_4_out, multiplexer_5_out;

  Multiplexer multiplexer_1 (.sel(LOAD), .in_0(INA), .in_1(DIN), .out(multiplexer_1_out));
  // Probe ASLL on d_ff_1_q
  D_FF d_ff_1 (.D(multiplexer_1_out), .C(CLK), .Q(d_ff_1_q));  // open: nQ
  Multiplexer multiplexer_2 (.sel(LOAD), .in_0(INB), .in_1(d_ff_1_q), .out(multiplexer_2_out));
  // Probe BSLL on d_ff_2_q
  D_FF d_ff_2 (.D(multiplexer_2_out), .C(CLK), .Q(d_ff_2_q));  // open: nQ
  Multiplexer multiplexer_3 (.sel(LOAD), .in_0(INC), .in_1(d_ff_2_q), .out(multiplexer_3_out));
  // Probe CSLL on d_ff_3_q
  D_FF d_ff_3 (.D(multiplexer_3_out), .C(CLK), .Q(d_ff_3_q));  // open: nQ
  Multiplexer multiplexer_4 (.sel(LOAD), .in_0(IND), .in_1(d_ff_3_q), .out(multiplexer_4_out));
  // Probe DSLL on d_ff_4_q
  D_FF d_ff_4 (.D(multiplexer_4_out), .C(CLK), .Q(d_ff_4_q));  // open: nQ
  Multiplexer multiplexer_5 (.sel(LOAD), .in_0(INE), .in_1(d_ff_4_q), .out(multiplexer_5_out));
  // Probe ESLL on d_ff_5_q
  D_FF d_ff_5 (.D(multiplexer_5_out), .C(CLK), .Q(d_ff_5_q));  // open: nQ
endmodule
